# Fritzing sketch RFID3 (saved by Fritzing 0.9.2b)

parts:
  RGB_LED_DFR0239 = RGB LED (com. cathode, rgb) [package="5 mm [THT]"]
  R5 = Resistor [tolerance=±5% resistance=1k package=THT]
  RelayModule_DFR0017 = RelayModule DFR0017
  WeMos_D1_Mini_or_DFRobot_WT8266-S1 = WeMos D1 Mini
  RS485_module_e_g_DFR0259 = MAX485 Breakout [chip_label=? package=THT]
  RS485_module_e_g_DFR0259_2 = MAX485 Breakout [chip_label=? package=THT]
  DFRuino_pro_mini = mini Arduino Pro
  DFrobot_NFC_module = RFID-RC522-v2
  Matrix_keypad_(DFRobot_FIT0129) = KEYPAD 4x4
  PushButton_e_g_DFRobot_FIT0115-G = DigitalPushButtonV2
  Buzzer_DFR0032 = BuzzerDFR0032

nets:
  N1: RGB_LED_DFR0239.red_anode, DFRuino_pro_mini.D8
  GND: RGB_LED_DFR0239.common_cathode, RGB_LED_DFR0239.green_anode, RS485_module_e_g_DFR0259.GND, DFRuino_pro_mini.GND, DFrobot_NFC_module.GND
  N2: RGB_LED_DFR0239.blue_anode, DFRuino_pro_mini.D9
  N3: R5.Pin_0, PushButton_e_g_DFRobot_FIT0115-G.Input
  3V3: R5.Pin_1, WeMos_D1_Mini_or_DFRobot_WT8266-S1.3V3, RS485_module_e_g_DFR0259_2.VCC
  N4: RelayModule_DFR0017.5V, WeMos_D1_Mini_or_DFRobot_WT8266-S1.D4
  N5: WeMos_D1_Mini_or_DFRobot_WT8266-S1.D1, RS485_module_e_g_DFR0259_2.RE, RS485_module_e_g_DFR0259_2.DE
  N6: WeMos_D1_Mini_or_DFRobot_WT8266-S1.D2, PushButton_e_g_DFRobot_FIT0115-G.Signal
  N7: WeMos_D1_Mini_or_DFRobot_WT8266-S1.G, RS485_module_e_g_DFR0259_2.GND
  N8: WeMos_D1_Mini_or_DFRobot_WT8266-S1.RX, RS485_module_e_g_DFR0259_2.RO
  N9: WeMos_D1_Mini_or_DFRobot_WT8266-S1.TX, RS485_module_e_g_DFR0259_2.DI
  N10: RS485_module_e_g_DFR0259.RO, DFRuino_pro_mini.RXI
  N11: RS485_module_e_g_DFR0259.RE, RS485_module_e_g_DFR0259.DE, DFRuino_pro_mini.D6
  N12: RS485_module_e_g_DFR0259.DI, DFRuino_pro_mini.TXO
  N13: RS485_module_e_g_DFR0259.VCC, DFRuino_pro_mini.VCC#11
  N14: DFRuino_pro_mini.D10, DFrobot_NFC_module.SDA
  N15: DFRuino_pro_mini.D11, DFrobot_NFC_module.MOSI
  N16: DFRuino_pro_mini.D12, DFrobot_NFC_module.MISO
  N17: DFRuino_pro_mini.D13, DFrobot_NFC_module.SCK
  N18: DFRuino_pro_mini.A1, Matrix_keypad_(DFRobot_FIT0129).col1
  N19: DFRuino_pro_mini.A2, Matrix_keypad_(DFRobot_FIT0129).col2
  N20: DFRuino_pro_mini.A3, Matrix_keypad_(DFRobot_FIT0129).col3
  N21: DFRuino_pro_mini.A4, Matrix_keypad_(DFRobot_FIT0129).col4
  N22: DFRuino_pro_mini.VCC#17, DFrobot_NFC_module.3.3V
  N23: DFRuino_pro_mini.D2, Matrix_keypad_(DFRobot_FIT0129).row1
  N24: DFRuino_pro_mini.D3, Matrix_keypad_(DFRobot_FIT0129).row2
  N25: DFRuino_pro_mini.D4, Matrix_keypad_(DFRobot_FIT0129).row3
  N26: DFRuino_pro_mini.D5, Matrix_keypad_(DFRobot_FIT0129).row4
  N27: DFRuino_pro_mini.D7, Buzzer_DFR0032.Signal

notes:
  Prog
  Buzzer

custom parts:
  WeMos D1 Mini: The D1 mini is a mini wifi board based on ESP-8266EX.
  MAX485 Breakout: MAX485 RS485 breakout board
  RFID-RC522-v2: A simple China made RFID-RC522 Reader; do check the pin labels, as this is a MFRC522 based clone.
  KEYPAD 4x4: Matrix keypad 16 buttons, 4 rows x 4 columns

// code stored in the sketch: RFID-D1.h.ino
#define WIFI_SSID "my_wifi"
#define WIFI_PASS "password"
#define MQTT_SERV "111.222.333.444" 
#define MQTT_PORT 1883
#define MQTT_USER "username"
#define MQTT_PASS "pass"
#define MQTT_TOPC "logTopic"


//#define SOFT_SERIAL
#undef SOFT_SERIAL


#define DE D1
#define RE D1
#define OPEN_PIN D4
#define KEY_PIN D2
#define SPEED 9600


#define BUF_SIZE 1024
#define IMPULSE 400
#define DELAY 100

#define KBD 1
#define CARD 2

#define STARTER '_'
#define ENDER '~'

#define Waiting 0
#define NewCard 1
#define Program 2
#define Other   3

#define SEQ_LEN 4

// code stored in the sketch: RFID-D1.ino
/*
  Control side.
  Use Wemos D1 of any other ESP8266 module with enough pins
*/
#include "RFID_D1.h"

#include <ESP8266WiFi.h>
#include <PubSubClient.h>
#include "SoftwareSerial.h"

#ifdef SOFT_SERIAL
#define RX D1
#define TX D2
#endif

static char buffer[BUF_SIZE];

static int mode=
/*
#define MQTT_SERV "m21.cloudmqtt.com"
#define MQTT_PORT 1883
#define MQTT_USER "123123123"
#define MQTT_PASS "qweqweqwe"
#define MQTT_TOPC "logTopic"
*/

char secret_open[SEQ_LEN]="1234";    //reverse! real sequence will be 4321
//char secret_new[]="*5544*";   // add card !reverse!
//char secret_del[]="*8899*";   // del card !reverse!
//char secret_clear[]="*0000*"; // del all !reverse!

#define NUM_CODES 16
emun fazes={ AddCardStart, AddCardNumber, DelCardStart, DelCardNumber,
             Open, None};
#define BAD_CARD 879961
#define IND_INTERVAL 300


void do_open(){
    digitalWrite(OPEN_PIN, HIGH);
    delay(IMPULSE);
    digitalWrite(OPEN_PIN, LOW);
    do_log("Opened!");
    do_log_send();
}
void do_close(){
    digitalWrite(OPEN_PIN, LOW);
}

void clear_all();
void do_program(const char *entered);
void write_open_seq(const char *seq);
void read_open_seq();

/*
 * *************************************************
 * 
 * 
 * 
 */
 
WiFiClient espClient;
PubSubClient client(espClient);
long lastMsg = 0;
char msg[50];
int value = 0;
#ifdef SOFT_SERIAL
SoftwareSerial mySerial(RX, TX);
#else
  #define mySerial Serial
#endif

static char log_buffer[1024]="";

void do_log_send(){
  if(!client.publish(MQTT_TOPC, log_buffer)){
    debug("publish fail...");
  }
  log_buffer[0]='\0';
}
void do_log(const char *s){
  strcat(log_buffer,s);
}

void debug(const char *s){
//  Serial.println(s);
}

void debug0(const char *s){
//  Serial.print(s);
}

#define DIR_OUT HIGH
#define DIR_IN  LOW

void set_dir(int d){
  digitalWrite(RE, d);
  digitalWrite(DE, d);  
}

void setup() {
  pinMode(OPEN_PIN,  OUTPUT);
  digitalWrite(OPEN_PIN, LOW);
  do_close();
  pinMode(RE,   OUTPUT);
  pinMode(DE,   OUTPUT);
  set_dir(DIR_IN);

  //Serial.begin(SPEED);
  ESP.wdtDisable();
  ESP.wdtEnable(WDTO_8S);


  ESP.wdtFeed();
  
  setup_wifi();
  client.setServer(MQTT_SERV, MQTT_PORT);
  client.setCallback(callback);
  reconnect();

  ESP.wdtFeed();
  debug("MySerial...");
  mySerial.begin(SPEED);
  //ESP.wdtFeed();
  do_log("Start!\n");
  do_log_send();

  read_open_seq();
}

void setup_wifi() {

  delay(10);
  // We start by connecting to a WiFi network
  //Serial.println();
  debug0("Connecting to ");
  debug(WIFI_SSID);
  yield();

  WiFi.begin(WIFI_SSID, WIFI_PASS);

  while (WiFi.status() != WL_CONNECTED) {
    yield();
    delay(500);
    debug0(".");
  }

  debug("WiFi connected");
  debug0("IP address: ");
  debug(WiFi.localIP().toString().c_str());
}

void callback(char* topic, byte* payload, unsigned int length) {
  debug0("Message arrived [");
  debug0(topic);
  debug0("] ");
  for (int i = 0; i < length; i++) {
    buffer[i]=(char)payload[i];
  }
  buffer[length]='\0';
  debug(buffer);

  // Switch on the LED if an 1 was received as first character
  if ((char)payload[0] == '1') {
    do_open();
  }

}

void reconnect() {
  //return;

  // Loop until we're reconnected
  while (!client.connected()) {
    debug0("Attempting MQTT connection...");
    // Attempt to connect
    if (client.connect(MQTT_SERV, MQTT_USER, MQTT_PASS)) {
      debug("connected");
      // Once connected, publish an announcement...
      //!client.publish("outTopic", "hello world");
      // ... and resubscribe
      client.subscribe("inTopic");
    } else {
      debug0("failed, rc=..");
      //debug0(client.state());
      debug(" try again in 5 seconds");
      // Wait 5 seconds before retrying
      delay(5000);
    }
    ESP.wdtFeed();
  }
}

// get new char from mySerial if avilable
int checkChar(){
  if(mySerial.available()){
    return mySerial.read();
  }
  return -1;
}

void do_send(const char *s){
  set_dir(DIR_OUT);
  delay(10);
  mySerial.println(s);
  delay(100);
  set_dir(DIR_IN);
  delay(10);
}

void process_extra(const char *s){
  do_log("Extra: ");
  do_log(s);
  do_log_send();
}

void process_message(const char *s){
  char *entered;
  short msg_type=0;
  do_log("Msg: ");
  do_log(s);
  do_log_send();

  if(strncmp(s,"Buffer=",7)==0){
    entered=s+7;
    msg_type=KBD;
  }
  if(strncmp(s,"CUID=",7)==0){
    entered=s+7;
    msg_type=CARD;
  }
     // do action using bringed card and mode
  switch(mode){
    case Waiting:
      if(msg_type==KBD){
        check_kbd(entered);
      }else if(msg_type==CARD){
        check_code(entered);
      }
      break;
    case Program:
      do_program(entered);
    default:
      send_it0("!invalid mode=");
      send_it(mode);
  }
}

void ind_success(){
  do_send("+p+g");
  delay(IND_INTERVAL);
  ind_none();
}

void ind_cancel(){
  do_send("+p+r");
  delay(IND_INTERVAL);
  ind_none();
}

void ind_input(){
  do_send("+r+g");
}

void ind_none(){
  do_send("-r-g-b");
}

void check_kbd(const char *entered){
  if(strncmp(secret_new,entered,strlen(secret_new))==0){
    mode=NewCard;
  }
  else if(strncmp(secret_del,entered,strlen(secret_del))==0){
    del_code();
    mode=Waiting;
  }
  else if(strncmp(secret_clear,entered,strlen(secret_clear))==0){
    clear_all();
    mode=Waiting;
  }
  else if(strncmp(secret_open,entered,strlen(secret_open))==0){
    do_open();
    mode=Waiting;
  }
}

void checkInput(){
  static char buf[BUF_SIZE];
  static int i=0;
  static int c;

  for(c=checkChar(); c!=-1; c=checkChar()){
    buf[i]=(char)c;
    i+=1;
    if(c==ENDER){
        buf[i-1]='\0';
        process_message(buf);
        i=0;
    }
    if(c==STARTER){
      if(i>1){
        buf[i-1]='\0';
        process_extra(buf);
        //do_send("zzz");
      }
      i=0;
    }
  }
}

// check card (1=success, 0=fail)
int check_code(const char *s){
  unsigned long id=0;
  int len=strlen(s);
  static unsigned long saved;

  for(int i=0;i<len;++i){
    if(*s<='9' && *s>='0'){
      id=id*16+(int)*s-(int)'0';
    }
    else{
      id=id*16+(int)*s-(int)'A';
    }
  }
  for(int i=1;i<=num_codes; ++i){
    EEPROM.get(i*ulen,saved);
    if(saved==id){
      send_it0("Card index=");
      send_it(i-1);
      do_send("+g");
      do_open();
      delay(1000);
      do_send("-g");
      return 1;
    }
  }
  do_send("+r"); //red
  do_send("+p"); //beep
  delay(1000);
  do_send("-r");

  return 0;
}


void loop() {
  static int c;
  static int count=0;

  yield();
  ESP.wdtFeed();
  if (!client.connected()) {
    reconnect();
  }
  client.loop();

  delay(DELAY);
  checkInput();

  // if 'program' pressed?
  pressed=analogRead(KEY_PIN);
  if(pressed>100){
    delay(100); // DUMMY DEBOUNCE
    send_it("Program mode");
    mode=Program;
    return;
  }
}

void read_open_seq(){
  for(int i=0;i<SEQ_LEN;++i)
    EEPROM.get(OPEN_ADDR+i,secret_open[i]);
}

void write_open_seq(const char *seq){
  for(int i=0;i<SEQ_LEN;++i)
    EEPROM.put(OPEN_ADDR+i,secret_open[i]);
}


void do_program(const char *entered){
  static int faze=None;
  static int index;

  switch(faze){
    case None:
      switch(entered[0]){
        case '*':  //add card
          //add card
          faze=AddCardStart;
          ind_input();
          break;
        case '#':
          //delete card
          faze=DefCardStart;
          ind_input();
          break;
        case  '0':
          // del all cards
          clear_all();
          mode=Waiting;
          break;
        case 'D': // new open sequence
          faze=Open;
          index=0;
          ind_input();
          break;
        default:
          mode=Waiting;
         // indication...
      }
      break;
    case AddCardStart:
      tone1();
      if(entered[0]=='*' || entered[0]=='#'){
        ind_cancel();
        mode=Waiting;
        faze=None;
        ind_none();
        return;
      }
      index=entered[0]-'0';
      if(index>9){
        index=index+'0'-'A'+10;
      }
      index+=1;
      faze=AddCardNumber;
      break;
    case AddCardNumber:
      if(entered[0]=='*' || entered[0]=='#'){
        ind_cancel();
        mode=Waiting;
        faze=None;
        ind_none();
        return;
      }
      if(index>num_codes)
        num_codes=index;
      EEPROM.put(index*ulen,entered);
      ind_success();
      mode=Waiting;
      faze=None;
    case DelCardStart:
      tone1();
      if(entered[0]=='*' || entered[0]=='#'){
        ind_cancel();
        mode=Waiting;
        faze=None;
        ind_none();
        return;
      }
      index=entered[0]-'0';
      if(index>9){
        index=index+'0'-'A'+10;
      }
      index+=1;
      faze=DelCardNumber;
      break;
    case DelCardNumber:
      if(entered[0]=='*' || entered[0]=='#'){
        ind_cancel();
        mode=Waiting;
        faze=None;
        ind_none();
        return;
      }
      if(index>num_codes)
        num_codes=index;
      EEPROM.put(key*ulen,BAD_CARD);
      ind_success();
      mode=Waiting;
      faze=None;
    case Open: // next leter of new code
      secret_open[index]=entered[0];
      index+=1;
      if(index>=SEQ_LEN){
        mode=Waiting;
        faze=None;
        ind_success();
        write_open_seq(secret_open);
      }
      break;
    default:
      mode=Waiting;
  }
}

// erase all cards!!!
void clear_all(){
  EEPROM.put(0, 0L);// zero cards
  for(int i=0;i<NUM_CODES;++i){
    EEPROM.put((i+1)*ulen, BAD_CARD);
  }
  num_codes=0;
}

// code stored in the sketch: RFID2.ino
/*
 * Digital lock with keyboard (4x4) and NFC.
 * 16 cards are supported. To add card, press 'program' key,
 * then '*' on keyboard, bring the card, them press number,
 * corresponding to this card index.
 * To delete card, press 'program' key, then '#', then card index.
 * To delete ALL cards, press 'program', then '0'.
 * To write open sequence, press 'program', then 'D',
 * then 4 keys of sequence (length can be changed in SEQ_LEN).
 * 
 * Card index can be 0-9 and A-D.
 * 
 * You can change values of secret_*** variables to set sequences
 * for add/del cards without 'program' key. It is INSECURE and not
 * recommended.
 * 
 * Connections:
 * MFRC522:
 *  NSS = 10
 *  SCK = 13
 *  MOSI = 11
 *  MISO = 12
 * 
 * Keyboard:
 *  pins 2-9 = 0..*
 * 
 * A0 = open
 * A1 = blue LED
 * A2 = green LED
 * A3 = red LED
 * A4 = program
 * A5 = buzzer
 * 
 */


#include "pitches.h"

#include <EEPROM.h>

#include <Keypad.h>

#include <SPI.h>
#include <MFRC522.h>
//
// NSS = 10
// SCK = 13
// MOSI = 11
// MISO = 12
// 



#define SS_PIN 10
#define RST_PIN 9
MFRC522 mfrc522(SS_PIN, RST_PIN);       // ?????? MFRC522
unsigned long uidDec, uidDecTemp;       // ??? ??????????? ?????? ???????? ? ?????????? ???????
byte bCounter, readBit;
unsigned long ticketNumber;

const byte ROWS = 4; // 4 ??????
const byte COLS = 4; // 4 ???????
char keys[ROWS][COLS] = {
  {'1','2','3','A'},
  {'4','5','6','B'},
  {'7','8','9','C'},
  {'*','0','#','D'}
}; 
byte rowPins[ROWS] = {9, 8, 7, 6}; 
byte colPins[COLS] = {5, 4, 3, 2}; 
Keypad keypad = Keypad( makeKeymap(keys), rowPins, colPins, ROWS, COLS );

char entered[16]="x";
char secret_open[]="5173";    //reverse! real sequence will be 3715
char secret_new[]="x*1425*";   // add card !reverse!
char secret_del[]="x*7765*";   // del card !reverse!
char secret_clear[]="x*0921*"; // del all !reverse!

#define NUM_CODES 16
#define OPENER A0
#define IPIN1 A1
#define IPIN2 A2
#define IPIN3 A3
#define KEY_PIN A4

#define RED IPIN3
#define GREEN IPIN2
#define BLUE IPIN1

#define BUZZER A5
#define NOTE1 NOTE_A2
#define BUZ_TIME 50

#define OPEN_TIME 500
#define NONVALID 90909090L

#define Waiting 0
#define NewCard 10
#define DelCard 20
#define NewCode 30
#define Clear   40
#define Program 50

#define OPEN_ADDR 500
#define SEQ_LEN 4

unsigned long codes[NUM_CODES];
unsigned long num_codes;
short int mode=Waiting;

const int ulen=sizeof(unsigned long);

void setup() {
  Serial.begin(9600);     
  SPI.begin();            // init SPI
  mfrc522.PCD_Init();     // init MFRC522
  Serial.println(F("Starting..."));

  EEPROM.get(0, num_codes);
  if(num_codes>NUM_CODES)
    num_codes=NUM_CODES;

  // read all cards
  for(int i=0;i<num_codes;++i){
    EEPROM.get((i+1)*ulen, codes[i]);
  }

  // init pins
  pinMode(OPENER, OUTPUT);
  pinMode(KEY_PIN, INPUT);
  pinMode(IPIN1, OUTPUT);
  pinMode(IPIN2, OUTPUT);
  pinMode(IPIN3, OUTPUT);
  pinMode(BUZZER, OUTPUT);
  analogWrite(OPENER,0);
  analogWrite(IPIN1, 0);
  analogWrite(IPIN2, 0);
  analogWrite(BUZZER, 0);

  read_open_seq();

  // salute by leds!
  //tone1();
  analogWrite(IPIN1, 256);
  delay(500);
  analogWrite(IPIN1, 0);
  analogWrite(IPIN2, 256);
  delay(500);
  analogWrite(IPIN2, 0);
  analogWrite(IPIN3, 256);
  delay(500);
  analogWrite(IPIN3, 0);
}

void read_open_seq(){
  for(int i=0;i<SEQ_LEN;++i)
    EEPROM.get(OPEN_ADDR+i,secret_open[i]);
}

void write_open_seq(const char *seq){
  for(int i=0;i<SEQ_LEN;++i)
    EEPROM.put(OPEN_ADDR+i,secret_open[i]);
}

// key pressed, add it to buffer
void add_key(char key){
  //shift!
  for(int i=sizeof(entered)-1;i>0;--i){
    entered[i]=entered[i-1];
  }
  entered[0]=key;
}

void leds_off(){
  analogWrite(IPIN1, 0);
  analogWrite(IPIN2, 0);
  analogWrite(IPIN3, 0);  
}

// indicate idle mode
void ind_waiting(){
  leds_off();
  Serial.println(F("waiting mode..."));
}

// indicate waiting for card index enter (blue led)
void ind_get_index(){
  Serial.println(F("Enter index:"));
  leds_off();
  analogWrite(BLUE, 255);
}

// indicate success (short green led flash, beep)
void ind_success(){
  Serial.println(F("Success!"));
  leds_off();
  analogWrite(GREEN, 255);
  tone1();
  delay(300);
  analogWrite(GREEN, 0);
}

// indicate operation cancelling (short magenta flash)
void ind_cancel(){
  Serial.println(F("Cancelled."));
  leds_off();
  analogWrite(BLUE, 255);
  analogWrite(RED, 255);
  delay(300);
  leds_off();
}

// indicate open (short green+blue flash)
void ind_opening(){
  Serial.println(F("Opening..."));
  leds_off();
  analogWrite(GREEN, 255);
  analogWrite(BLUE, 255);
  delay(300);
  leds_off();
}

// play short buzzer tone
void tone1(){
    tone(BUZZER, NOTE1, BUZ_TIME);
    delay(BUZ_TIME);
    noTone(BUZZER);  
}

// indicate fail (red led flash, two beeps)
void ind_failed(){
  Serial.println(F("Failed!"));
  leds_off();
  analogWrite(RED, 255);
  tone1();
  delay(100);
  tone1();
  delay(500);
  analogWrite(RED, 0);
}

// erase all cards!!!
void clear_all(){
  EEPROM.put(0, 0L);// zero cards
  for(int i=0;i<NUM_CODES;++i){
    EEPROM.put((i+1)*ulen, NONVALID);
  }
  num_codes=0;
}

// add new card
void add_code(unsigned long id){
  char key='\0';
  
  ind_get_index();

  while(!key){
    key = keypad.getKey();
    delay(10);
  }
  tone1();
  if(key=='*' || key=='#'){
    ind_cancel();
    return;
  }
  key-='0';
  if(key>9){
    key=key+'0'-'A'+10;
  }
  key+=1;
  if(key>num_codes)
    num_codes=key;
  EEPROM.put(key*ulen,id);
  ind_success();
  
  Serial.print(F("Added new card: "));
  Serial.println(key-1);

}

// delete card
void del_code(){
  char key='\0';
  
  Serial.println(F("Choose index"));

  while(!key){
    key = keypad.getKey();
    delay(10);
  }
  tone1();
  if(key=='*' || key=='#'){
    ind_cancel();
    return;
  }
  key-='0';
  if(key>9){
    key=key+'0'-'A'+10;
  }
  key+=1;
  EEPROM.put(key*ulen,NONVALID);
  ind_success();
  Serial.print(F("Deleted card: "));
  Serial.println(key-1);
}

// new open sequence
void new_seq(){
  static char key;
  
  Serial.println(F("New open sequence"));

  for(int i=SEQ_LEN-1; i>=0; --i){
    key='\0';
    while(!key){
      key = keypad.getKey();
      delay(100);
    }
    tone1();
    secret_open[i]=key;
  }
  secret_open[SEQ_LEN]='\0'; // for sure...
  write_open_seq(secret_open);
  ind_success();
  Serial.print(F("New reversed sequence: "));
  Serial.println(secret_open);
}

// check card (1=success, 0=fail)
int check_code(unsigned long id){
  static unsigned long saved;
  
  for(int i=1;i<=num_codes; ++i){
    EEPROM.get(i*ulen,saved);
    if(saved==id){
      Serial.print(F("Card index="));
      Serial.println(i-1);
      //Serial.println(F(". Opening..."));
      ind_success();
      return 1;
    }
  }
  ind_failed();
  return 0;
}

// open the door!!!
void do_open(){
  ind_opening();
  analogWrite(OPENER,255);
  delay(OPEN_TIME);
  analogWrite(OPENER,0);
}



void do_program(){
  if(entered[0]=='*'){  //add card
    //add card
    mode=NewCard;
  }
  else if(entered[0]=='#'){ // del card
    //delete card
    del_code();
    mode=Waiting;
  }
  else if(entered[0]=='0'){ // del all cards
    clear_all();
    mode=Waiting;
  }
  else if(entered[0]=='D'){  // new open sequence
    new_seq();
    mode=Waiting;
  }
  else{
    ind_cancel();
    mode=Waiting;  
  }
}

/******************************************************************
 * 
 *****************************************************************/

void loop() {
  static char key;
  static int pressed;
  
  key = keypad.getKey();
  if (key){
    //Serial.println(key);
    Serial.println(entered);
    tone1();
    add_key(key);
    if(mode==Program)
      return do_program();
    if(strncmp(secret_new,entered,strlen(secret_new))==0){
      Serial.println(F("Adding card!"));
      mode=NewCard;
    }
    else if(strncmp(secret_del,entered,strlen(secret_del))==0){
      Serial.println(F("Del card!"));
      del_code();
      mode=Waiting;
    }
    else if(strncmp(secret_clear,entered,strlen(secret_clear))==0){
      Serial.println(F("Clear all!"));
      clear_all();
      mode=Waiting;
    }
    else if(strncmp(secret_open,entered,strlen(secret_open))==0){
      Serial.println(F("Open!!"));
      do_open();
      mode=Waiting;
    }
  }

  // if 'program' pressed?
  pressed=analogRead(KEY_PIN);
  if(pressed>100){
    delay(100); // DUMMY DEBOUNCE
    Serial.println(F("Program!"));
    mode=Program;
    return;
  }
  
  // check for card bringing
  if( ! mfrc522.PICC_IsNewCardPresent()) {
    return;
  }
  Serial.println(F("Card bringed!"));
        
  // read card serial
  if ( ! mfrc522.PICC_ReadCardSerial()) {
    Serial.println(F("Cannot read serial!"));
    return;
  }

   uidDec = 0;

   // print card serial
   Serial.print(F("Card UID: "));
   for (byte i = 0; i < mfrc522.uid.size; i++) {
     // Serial.print(mfrc522.uid.uidByte[i] < 0x10 ? " 0" : " ");
     // Serial.print(mfrc522.uid.uidByte[i], HEX);
     uidDecTemp=mfrc522.uid.uidByte[i];
     uidDec=uidDec*256+uidDecTemp;
   } 
   Serial.println(uidDec);
   Serial.println();

   // do action using bringed card and mode
   switch(mode){
     case Waiting:
       if(check_code(uidDec)){
         do_open();
       }
       break;
     case NewCard:
       //Serial.println(F("--------->"));
       add_code(uidDec);
       mode=Waiting;
       break;
     default:
       Serial.print(F("invalid mode="));
       Serial.println(mode);
   }
}

/*************************************************
 * 
 * Unused code
 * 
 */








////////////////////////////////////////////////////////////////
//
//   Metro
//
////////////////////////////////////////////////////////////////
void printIssueDate(unsigned int incoming) {

boolean isLeap = true; // ??????? ??????????? ????
int days[]={0,31,59,90,120,151,181,212,243,273,304,334}; // ????????? ?? ??????? ???? ?????? ??? ???????? ????
byte dayOfMonth, monthCounter;
unsigned int yearCount;

incoming = incoming+1; // ???????? ??? ?????, ?? ???????? ??? ??? ??? ??????????? ?????????, ?????? ??? ?????? ??????? - 01.01.1992, ? ?? 00.01.1992

for (yearCount = 1992; incoming >366; yearCount++) { // ??????? ??? ? ?????????? ????, ????????? ? ?????? ??????

        if ((yearCount % 4 == 0 && yearCount % 100 != 0) ||  yearCount % 400 == 0) {
                incoming = incoming - 366;
                isLeap = true;
          } else {
                incoming = incoming - 365;
                isLeap = false;
                }
        }

for (monthCounter = 0; incoming > days[monthCounter]; monthCounter++) { // ?????? ????? ??????
}

// ??????? ???? ??????

if (isLeap == true) { // ???? ?????????? ???
  if (days[monthCounter-1]>31) { // ???? ?? ?????? ?????, ?? ????????? ? ?????????? ??? ?????? ???????
  dayOfMonth = incoming - (days[monthCounter-1]+ 1);
  } else {
    dayOfMonth = incoming - (days[monthCounter-1]); // ???? ?????? - ?????? ?? ?????????, ?????? ??? ????? ?????????? ? ???????
  }
} else {
  dayOfMonth = incoming - (days[monthCounter-1]); // ???? ?? ?????????? ???
}

Serial.print(dayOfMonth);
Serial.print(".");
Serial.print(monthCounter);
Serial.print(".");
Serial.print(yearCount);
Serial.println();

        

}




void setBitsForGood(byte daBeat) {


  
        if (daBeat == 1) {
                bitSet(ticketNumber, bCounter);
                bCounter=bCounter+1;
                }
        else {
                bitClear(ticketNumber, bCounter);
                bCounter=bCounter+1;
        }
}

void metro(){
        // ?????? ???? ?????
        MFRC522::PICC_Type piccType = mfrc522.PICC_GetType(mfrc522.uid.sak); // ?????? ????
        Serial.print("Card type: ");
        Serial.println(mfrc522.PICC_GetTypeName(piccType)); // ?????????? ???? ? ???????? ???
        
        if (piccType != MFRC522::PICC_TYPE_MIFARE_UL) { // ???? ?? ???????? ?????
                Serial.print("Not a valid card: "); // ??? ? ???????
                Serial.println(piccType);                               
                // Halt PICC
                mfrc522.PICC_HaltA();                   // ????????? ????
                return;
        }

// ???? ?? ???????, ???? ??? ??????????

        MFRC522::StatusCode status;
        byte byteCount;
        byte buffer[18]; // ????? ??????? (16 ???? + 2 ????? ??????????? ?????) 
        byte pages[2]={4, 8}; // ???????? ? ???????
        byte pageByte; // ??????? ?????? ????????
        
        byteCount = sizeof(buffer);
        byte bCount=0;
                

        for (byte i=0; i<2; i++) { // ???????? ?????? ????????
        status = mfrc522.MIFARE_Read(pages[i], buffer, &byteCount);
        
        if (status != MFRC522::STATUS_OK) {
                Serial.print("Read error: ");
                Serial.println(mfrc522.GetStatusCodeName(status));}
                else {
                      if (pages[i] == 4) {
                                bCounter = 0; // 32-?????? ??????? ??? ??????
                                
                                // ???? 0-3
                                for (bCount=0; bCount<4; bCount++) {
                                        readBit = bitRead(buffer[6], (bCount+4));
                                        setBitsForGood(readBit);
                                }

                                // ???? 4 - 27
                                for (pageByte=5; pageByte > 2; pageByte--) {
                                        for (bCount=0; bCount<8; bCount++) {
                                                readBit = bitRead(buffer[pageByte], bCount);
                                                setBitsForGood(readBit);
                                        }
                                }

                                // ???? 28-31
                                for (bCount=0; bCount<4; bCount++) {
                                        readBit = bitRead(buffer[2], bCount);
                                        setBitsForGood(readBit);
                                }

                                Serial.print("Ticket number: ");
                                Serial.println(ticketNumber, DEC);
                         }
                        
                          if (pages[i] == 8) { // ?????? ???? ??????

                                Serial.print("Issued: ");
                                unsigned int issueDate = buffer[0] * 256 + buffer[1]; // ?????????? ???? ? 01.01.1992 ? ?????????? ???????, 256 - ????? ?? 8 ???
                                printIssueDate(issueDate);

                                Serial.print("Good for (days): "); // ???? ????????
                                Serial.print(buffer[2], DEC);                                                           
                                Serial.println();                               
                        
                                Serial.print("Trip reminder: "); // ?????????? ?????????? ???????
                                Serial.print(buffer[5], DEC);                                                           
                                Serial.println();       
                        }
                        
                }
        }
        // Halt PICC
    mfrc522.PICC_HaltA();                         
}

// code stored in the sketch: RFID3-D1-pult2.ino
/*
 * Digital lock with keyboard (4x4) and NFC.
 * 16 cards are supported. To add card, press 'program' key,
 * then '*' on keyboard, bring the card, them press number,
 * corresponding to this card index.
 * To delete card, press 'program' key, then '#', then card index.
 * To delete ALL cards, press 'program', then '0'.
 * To write open sequence, press 'program', then 'D',
 * then 4 keys of sequence (length can be changed in SEQ_LEN).
 * 
 * Card index can be 0-9 and A-D.
 * 
 * You can change values of secret_*** variables to set sequences
 * for add/del cards without 'program' key. It is INSECURE and not
 * recommended.
 * 
 * Connections:
 * MFRC522:
 *  NSS = 10
 *  SCK = 13
 *  MOSI = 11
 *  MISO = 12
 * 
 * Keyboard:
 *  pins *..D -> A2-A5,D2-D5
 * 
 * D6 - serial direction
 * D7 - buzzer
 * D8 = RED LED
 * D9 = GREEN LED
 */

//#define DEBUG

#include "pitches.h"
#include <EEPROM.h>

#include <SPI.h>
#include <MFRC522.h>
//
// NSS = 10
// SCK = 13
// MOSI = 11
// MISO = 12
// 

#define SPEED 9600

#define SS_PIN 10
#define RST_PIN 9

MFRC522 mfrc522(SS_PIN, RST_PIN);       // объект MFRC522
unsigned long uidDec, uidDecTemp;       // для отображения номера карточки в десятичном формате
byte bCounter, readBit;
unsigned long ticketNumber;

#define DIRECTION 7
#define DIR2 7

#define ENTERED_LEN 8
char entered[ENTERED_LEN+1]="x";

#define LED_PIN A0

#define STARTER "_"
#define ENDER "~"

unsigned long codes[NUM_CODES];
unsigned long num_codes;
short int mode=Waiting;

const int ulen=sizeof(unsigned long);
//void read_open_seq();

void setup() {
  pinMode(DIRECTION, OUTPUT);
  digitalWrite(DIRECTION, LOW);
  pinMode(DIR2, OUTPUT);
  digitalWrite(DIR2, LOW);
  
  pinMode(LED_PIN, OUTPUT);
  analogWrite(LED_PIN,0);
  
  Serial.begin(SPEED);     
  SPI.begin();            // init SPI
  mfrc522.PCD_Init();     // init MFRC522
  mfrc522.PCD_SetAntennaGain(mfrc522.RxGain_max);
  send_it("Starting...");

  EEPROM.get(0, num_codes);
  if(num_codes>NUM_CODES)
    num_codes=NUM_CODES;

  // read all cards
  for(int i=0;i<num_codes;++i){
    EEPROM.get((i+1)*ulen, codes[i]);
  }

  init_keypad();

  read_open_seq();

  // salute by leds!
  tone1();
  analogWrite(IPIN1, 256);
  delay(300);
  analogWrite(IPIN1, 0);
  analogWrite(IPIN2, 256);
  delay(300);
  analogWrite(IPIN2, 0);
  analogWrite(IPIN3, 256);
  delay(300);
  analogWrite(IPIN3, 0);
  send_it("start");
}

/******************************************************************
 * 
 *****************************************************************/

void loop() {
  static char key;
  static int pressed;

//  if(Serial.available()){
//    char b[128]="Got: ";
//    int i=4;
//    while(Serial.available()){
//      b[i]=Serial.read();
//      i++;
//      delay(20);
//    }
//    b[i]='\0';
//    send_it(b);
//  }
  key=readdata();
  if (key!='X'){
    //Serial.println(key);
    //tone1();
    char str[2]=".";
    add_key(key);
    send_it0("Entered: ");
    send_it0(key);
    str[0]=key;
    send_it0("=");
    send_it(str);
    send_it0("Buffer=");
    send_it(entered);
  }
  //return;
  // check for card bringing

  check_card();
}

void turn_red(int on){
  digitalWrite(LED_RED, on==0 ? LOW : HIGH);
}
void turn_green(int on){
  digitalWrite(LED_GREEN, on==0 ? LOW : HIGH);
}
void turn_blue(int on){
  digitalWrite(LED_BLUE, on==0 ? LOW : HIGH);
}
void do_beep(int on){
  digitalWrite(BEEPER, HIGH);
  delay(BEEP_DELAY);
  digitalWrite(BEEPER, LOW);
}

void process_extra(const char *m){
  
}

void process_message(const char *m){
  if(strlen(m)!=2){
    send_it("!Bad msg");
    return;
  }
  switch(m[1]){
    case 'r':
      turn_red(m[0]=='+' ? 1 : 0);
    case 'g':
      turn_green(m[0]=='+' ? 1 : 0);
    case 'b':
      turn_blue(m[0]=='+' ? 1 : 0);
    case 'p': //beep
      do_beep();    
  }
}

// code stored in the sketch: RFID3_pult_helpers.ino
void process_extra(const char *);
void process_message(const char *);

#define RED D8
#define GREEN D9
#define BLUE D9

#define BUZZER D7

#define NOTE1 NOTE_A2
#define BUZ_TIME 50

#define OPEN_TIME 500
#define NONVALID 90909090L
#define DEBOUNCE 300

#define Waiting 0
#define NewCard 10
#define DelCard 20
#define NewCode 30
#define Clear   40
#define Program 50

#define OPEN_ADDR 500
#define SEQ_LEN 4


static char iobuf[128]="";
static char tmpbuf[128]="";

char mykeymap[4][4]={
  {'1','4','7','*'},
  {'2','5','8','0'},
  {'3','6','9','#'},
  {'A','B','C','D'}
};
const short KEYWRITE[]={A2,A3,A5,A4};
const short KEYREAD[]={3,4,5,6};




void send_it(const char *s){
  digitalWrite(DIRECTION, HIGH);
  delay(10);
  sprintf(iobuf,"%s%s%s%s",STARTER,tmpbuf,s,ENDER);
  Serial.write(iobuf);
  delay(100);
  digitalWrite(DIRECTION, LOW);
  tmpbuf[0]='\0';
  delay(10);
}

void send_it0(const char *s){
  strcat(tmpbuf,s);
}

void send_it(const long int s){
  char buf[16];
  sprintf(buf,"%ld",s);
  send_it(buf);
}

void send_it0(const long int s){
  char buf[16];
  sprintf(buf,"%ld",s);
  send_it0(buf);
}

void send_itH(const long int s){
  char buf[16];
  sprintf(buf,"%lX",s);
  send_it(buf);
}

void send_itH0(const long int s){
  char buf[16];
  sprintf(buf,"%lX",s);
  send_it0(buf);
}


void init_keypad(){
  for(int i=0;i<4;++i){
    pinMode(KEYREAD[i],INPUT_PULLUP);
  }
}

unsigned int getC(int index=-1)                   //determine whether there is 5V input on the analog pins 3-0
{
  int r;
  for(unsigned int i=0;i<4;++i){
    r=digitalRead(KEYREAD[i]);
    if(r==LOW){
      return i;
    }
  }
  return 255;
}

char readdata(void)          //main function
{
  unsigned int j;
  for (int i=0;i<4;i++){               //for loop
    analogWrite(KEYWRITE[i],0);
    j=getC(i);
    analogWrite(KEYWRITE[i],1024);
    if(j<255){
      delay(DEBOUNCE);
      return mykeymap[j][i];
    }   // output the char
  }
  return 'X';                  // if no button is pressed, return X
}

// key pressed, add it to buffer
void add_key(char key){
  //shift!
  for(int i=sizeof(entered)-1;i>0;--i){
    entered[i]=entered[i-1];
  }
  entered[0]=key;
  entered[sizeof(entered)-1]='\0';
}

void leds_off(){
//  analogWrite(IPIN1, 0);
//  analogWrite(IPIN2, 0);
//  analogWrite(IPIN3, 0);  
  analogWrite(LED_PIN, 0);
}

// indicate idle mode
void ind_waiting(){
  leds_off();
  send_it("waiting mode...");
}

// indicate waiting for card index enter (blue led)
void ind_get_index(){
  send_it("Enter index:");
  leds_off();
  analogWrite(BLUE, 255);
}

// indicate success (short green led flash, beep)
void ind_success(){
  send_it("Success!");
  leds_off();
  analogWrite(GREEN, 255);
  tone1();
  delay(300);
  analogWrite(GREEN, 0);
}

// indicate operation cancelling (short magenta flash)
void ind_cancel(){
  send_it("Cancelled.");
  leds_off();
  analogWrite(BLUE, 255);
  analogWrite(RED, 255);
  delay(300);
  leds_off();
}

// indicate open (short green+blue flash)
void ind_opening(){
  send_it("Opening...");
  leds_off();
  analogWrite(GREEN, 255);
  analogWrite(BLUE, 255);
  delay(300);
  leds_off();
}

// play short buzzer tone
void tone1(){
    tone(BUZZER, NOTE1, BUZ_TIME);
    delay(BUZ_TIME);
    noTone(BUZZER);  
}

/*
// indicate fail (red led flash, two beeps)
void ind_failed(){
  send_it("Failed!");
  leds_off();
  analogWrite(RED, 255);
  tone1();
  delay(100);
  tone1();
  delay(500);
  analogWrite(RED, 0);
}

// add new card
void add_code(unsigned long id){
  char key='\0';

  ind_get_index();

  for(key=readdata();key=='X';){
    delay(10);
  }
  tone1();
  if(key=='*' || key=='#'){
    ind_cancel();
    return;
  }
  key-='0';
  if(key>9){
    key=key+'0'-'A'+10;
  }
  key+=1;
  if(key>num_codes)
    num_codes=key;
  EEPROM.put(key*ulen,id);
  ind_success();
  
  send_it0("Added new card: ");
  send_it(key-1);

}

// delete card
void del_code(){
  char key='\0';
  
  send_it("Choose index");

  while(!key){
    //!!!key = keypad.getKey();
    delay(10);
  }
  tone1();
  if(key=='*' || key=='#'){
    ind_cancel();
    return;
  }
  key-='0';
  if(key>9){
    key=key+'0'-'A'+10;
  }
  key+=1;
  EEPROM.put(key*ulen,NONVALID);
  ind_success();
  send_it0("Deleted card: ");
  send_it(key-1);
}

// new open sequence
void new_seq(){
  static char key;
  
  send_it("New open sequence");

  for(int i=SEQ_LEN-1; i>=0; --i){
    key='\0';
    while(!key){
      //!!!key = keypad.getKey();
      delay(100);
    }
    tone1();
    secret_open[i]=key;
  }
  secret_open[SEQ_LEN]='\0'; // for sure...
  write_open_seq(secret_open);
  ind_success();
  send_it0("New reversed sequence: ");
  send_it(secret_open);
}
*/

//// open the door!!!
//void do_open(){
//  ind_opening();
//  digitalWrite(DIRECTION, HIGH);
//  delay(10);
//  Serial.println("@");
//  delay(100);
//  digitalWrite(DIRECTION, LOW);
////  analogWrite(OPENER,255);
////  delay(OPEN_TIME);
////  analogWrite(OPENER,0);
//}


/*
void do_program(){
  if(entered[0]=='*'){  //add card
    //add card
    mode=NewCard;
  }
  else if(entered[0]=='#'){ // del card
    //delete card
    del_code();
    mode=Waiting;
  }
  else if(entered[0]=='0'){ // del all cards
    clear_all();
    mode=Waiting;
  }
  else if(entered[0]=='D'){  // new open sequence
    new_seq();
    mode=Waiting;
  }
  else{
    ind_cancel();
    mode=Waiting;  
  }
}
*/

void check_card(MFRC522 &mfrc522){
  long int uidDec = 0L;

  if( ! mfrc522.PICC_IsNewCardPresent()) {
    return;
  }
  //send_it("Card bringed!");

  // read card serial
  if ( ! mfrc522.PICC_ReadCardSerial()) {
    send_it("Bad card");
    return;
  }

   // print card serial
   send_it0("CUID=");
   for (byte i = 0; i < mfrc522.uid.size; i++) {
     // Serial.print(mfrc522.uid.uidByte[i] < 0x10 ? " 0" : " ");
     // Serial.print(mfrc522.uid.uidByte[i], HEX);
     uidDecTemp=mfrc522.uid.uidByte[i];
     uidDec=uidDec*256+uidDecTemp;
   } 

   send_itH(uidDec);  
   mfrc522.PICC_HaltA(); // Stop reading
}

void checkInput(){
  static char buf[BUF_SIZE];
  static int i=0;
  static int c;

  for(c=checkChar(); c!=-1; c=checkChar()){
    buf[i]=(char)c;
    i+=1;
    if(c==ENDER){
        buf[i-1]='\0';
        process_message(buf);
        i=0;
    }
    if(c==STARTER){
      if(i>1){
        buf[i-1]='\0';
        process_extra(buf);
        //do_send("zzz");
      }
      i=0;
    }
  }
}
